# Fritzing sketch BoxBeatsSpectrum (saved by Fritzing 0.9.2b)

parts:
  Part1 = Arduino Uno (Rev3)  # not connected
  Part2 = SparkFun Spectrum Shield [part_number=DEV-13116]
  NEOPIXEL1 = Neopixel Strip -- White (60/m)
  NEOPIXEL2 = Neopixel Strip -- White (60/m)
  ENCODER1 = Rotary Encoder with Knob

nets:
  N1: Part2.D0, Part2.pin_172, ENCODER1.no_name_yet#1
  N2: Part2.D1, Part2.pin_140, ENCODER1.no_name_yet#3
  N3: Part2.D3, NEOPIXEL2.+5V
  N4: Part2.D10, Part2.pin_178, ENCODER1.no_name_yet#4
  N5: Part2.VIN, NEOPIXEL1.DI, NEOPIXEL2.DI
  GND: Part2.GND, NEOPIXEL1.GND, NEOPIXEL2.GND
  N6: Part2.pin_146, Part2.pin_157, ENCODER1.no_name_yet#2, ENCODER1.no_name_yet#5
  N7: Part2.D6, NEOPIXEL1.+5V

custom parts:
  SparkFun Spectrum Shield: This shield can be used to create sound visualizers, detect patterns in music or add sound activation to your microcontroller projects.
  Neopixel Strip -- White (60/m): Neopixel Strip, White, 60 pixels per meter.
  Rotary Encoder with Knob: Rotary Encoder with 1/4" Shaft and Knob
